# Fritzing sketch BeeModule (saved by Fritzing 1.0.4)
breadboards: 1

parts:
  WeMos_D1_Mini1 = WeMos D1 Mini
  Part1 = Humidity Temperature Sensor SHT15
  R1 = Resistor [tolerance=±5% resistance=220 package="0402 [SMD]"]
  BAT1 = BC9VPC [package=bc9vpc]
  U1 = MAX1555 Lithium Charger IC [package=sot23-5]  # not connected

nets:
  3V3: WeMos_D1_Mini1.3V3, Part1.VCC, BAT1.V+
  N1: WeMos_D1_Mini1.D6, Part1.SCL
  N2: WeMos_D1_Mini1.D7, Part1.SDA
  N3: WeMos_D1_Mini1.G, R1.Pin_1, BAT1.V-
  N4: Part1.GND, R1.Pin_0
